// Digital circuit ALU.dig as structural Verilog
module ALU (
  input  [7:0] A,
  input  [7:0] B,
  input  [2:0] Select,
  input  CLK,
  output [7:0] S,
  output [7:0] MQ,
  output [7:0] AC,
  output [7:0] MQ_2
);

  wire [7:0] div_1_r, MQ0, MQ1, multiplicador_8bit_1_p3, nand_1_s, shiftleft_8bits_1_out,
       shiftright_8bits_1_out, soma_8bit_1_s, \subtração_8bits_1_s , xor_8bits_1_s;

  soma_8bit soma_8bit_1 (.A(A), .B(B), .Cin(1'b0), .S(soma_8bit_1_s));  // open: Cout
  \subtração_8bits  \subtração_8bits_1  (.A(A), .B(B), .Cin(1'b0), .S(\subtração_8bits_1_s ));  // open: Cout
  // multiplicador_8bit multiplicador_8bit_1: pin names not known; wires that end beside it: A, B, {MQ0, multiplicador_8bit_1_p3}
  NAND nand_1 (.A(A), .B(B), .S(nand_1_s));
  xor_8bits xor_8bits_1 (.A(A), .B(B), .S(xor_8bits_1_s));
  shiftLeft_8bits shiftleft_8bits_1 (.in(A), .out(shiftleft_8bits_1_out));
  shiftRight_8bits shiftright_8bits_1 (.in(A), .out(shiftright_8bits_1_out));
  Div #(.Bits(8)) div_1 (.a(A), .b(B), .q(MQ1), .r(div_1_r));
  Multiplexer #(.Bits(8), .Selector_Bits(3)) multiplexer_1 (
    .sel(Select), .in_0(soma_8bit_1_s), .in_1(\subtração_8bits_1_s ), .in_2(multiplicador_8bit_1_p3),
    .in_3(nand_1_s), .in_4(xor_8bits_1_s), .in_5(shiftleft_8bits_1_out), .in_6(shiftright_8bits_1_out),
    .in_7(div_1_r), .out(S));
  Register #(.Bits(8)) u_MQ (.D(MQ1), .C(CLK), .en(1'b1), .Q(MQ));
  Register #(.Bits(8)) u_MQ_2 (.D(MQ0), .C(CLK), .en(1'b1), .Q(MQ_2));
  Register #(.Bits(8)) u_AC (.D(S), .C(CLK), .en(1'b1), .Q(AC));
endmodule
