// Digital circuit multiplicador-2bits.dig as structural Verilog
module multiplicador_2bits (
  input  [1:0] in_1,
  input  [1:0] in_2,
  output [3:0] out_3
);

  wire and_2_out, and_3_out, and_4_out, soma_1bit_1_cout;

  and and_1 (out_3[0], in_1[0], in_2[0]);
  and and_2 (and_2_out, in_1[0], in_2[1]);
  and and_3 (and_3_out, in_1[1], in_2[0]);
  and and_4 (and_4_out, in_1[1], in_2[1]);
  soma_1bit soma_1bit_1 (.A(and_2_out), .B(and_3_out), .Cin(1'b0), .S(out_3[1]), .Cout(soma_1bit_1_cout));
  soma_1bit soma_1bit_2 (.A(soma_1bit_1_cout), .B(and_4_out), .Cin(1'b0), .S(out_3[2]), .Cout(out_3[3]));

  // Other names for the same wires on the sheet: A0 = in_1[0]; A1 = in_1[1]; B0 = in_2[0]; B1 = in_2[1]
endmodule
