// Digital circuit soma-4bit.dig as structural Verilog
module soma_4bit (
  input  [3:0] A,
  input  [3:0] B,
  input  Cin,
  output [3:0] S,
  output Cout
);

  wire soma_1bit_1_cout, soma_1bit_2_cout, soma_1bit_3_cout;

  soma_1bit soma_1bit_1 (.A(A[0]), .B(B[0]), .Cin(Cin), .S(S[0]), .Cout(soma_1bit_1_cout));
  soma_1bit soma_1bit_2 (.A(A[1]), .B(B[1]), .Cin(soma_1bit_1_cout), .S(S[1]), .Cout(soma_1bit_2_cout));
  soma_1bit soma_1bit_3 (.A(A[2]), .B(B[2]), .Cin(soma_1bit_2_cout), .S(S[2]), .Cout(soma_1bit_3_cout));
  soma_1bit soma_1bit_4 (.A(A[3]), .B(B[3]), .Cin(soma_1bit_3_cout), .S(S[3]), .Cout(Cout));

  // Other names for the same wires on the sheet: Ci = Cin
endmodule
