// Digital circuit soma-8bit.dig as structural Verilog
module soma_8bit (
  input  [7:0] A,
  input  [7:0] B,
  input  Cin,
  output [7:0] S,
  output Cout
);

  wire soma_4bit_1_cout;

  soma_4bit soma_4bit_1 (.A(A[3:0]), .B(B[3:0]), .Cin(Cin), .S(S[3:0]), .Cout(soma_4bit_1_cout));
  soma_4bit soma_4bit_2 (.A(A[7:4]), .B(B[7:4]), .Cin(soma_4bit_1_cout), .S(S[7:4]), .Cout(Cout));

  // Other names for the same wires on the sheet: A0[3:0] = A[3:0]; A1[3:0] = A[7:4]; B0[3:0] = B[3:0];
  //   B1[3:0] = B[7:4]; S0[3:0] = S[3:0]; S1[3:0] = S[7:4]
endmodule
