// Digital circuit subtração-1bit.dig as structural Verilog
module \subtração_1bit  (
  input  A,
  input  B,
  input  Cin,
  output S,
  output Cout
);

  wire and_1_out, and_2_out, and_3_out, not_1_out, not_2_out;

  not not_1 (not_1_out, A);
  not not_2 (not_2_out, A);
  xor xor_1 (S, A, B, Cin);
  and and_1 (and_1_out, not_1_out, B);
  and and_2 (and_2_out, not_2_out, Cin);
  and and_3 (and_3_out, B, Cin);
  or or_1 (Cout, and_1_out, and_2_out, and_3_out);

  // Other names for the same wires on the sheet: Ci = Cin
endmodule
