// Digital circuit subtração-4bits.dig as structural Verilog
module \subtração_4bits  (
  input  [3:0] A,
  input  [3:0] B,
  input  Cin,
  output [3:0] S,
  output Cout
);

  wire \subtração_1bit_1_cout , \subtração_1bit_2_cout , \subtração_1bit_3_cout ;

  \subtração_1bit  \subtração_1bit_1  (.A(A[0]), .B(B[0]), .Cin(Cin), .S(S[0]), .Cout(\subtração_1bit_1_cout ));
  \subtração_1bit  \subtração_1bit_2  (
    .A(A[1]), .B(B[1]), .Cin(\subtração_1bit_1_cout ), .S(S[1]), .Cout(\subtração_1bit_2_cout ));
  \subtração_1bit  \subtração_1bit_3  (
    .A(A[2]), .B(B[2]), .Cin(\subtração_1bit_2_cout ), .S(S[2]), .Cout(\subtração_1bit_3_cout ));
  \subtração_1bit  \subtração_1bit_4  (.A(A[3]), .B(B[3]), .Cin(\subtração_1bit_3_cout ), .S(S[3]), .Cout(Cout));

  // Other names for the same wires on the sheet: Ci = Cin
endmodule
