// Digital circuit subtração-8bits.dig as structural Verilog
module \subtração_8bits  (
  input  [7:0] A,
  input  [7:0] B,
  input  Cin,
  output Cout,
  output [7:0] S
);

  wire \subtração_4bits_1_cout ;

  \subtração_4bits  \subtração_4bits_1  (
    .A(A[3:0]), .B(B[3:0]), .Cin(Cin), .S(S[3:0]), .Cout(\subtração_4bits_1_cout ));
  \subtração_4bits  \subtração_4bits_2  (
    .A(A[7:4]), .B(B[7:4]), .Cin(\subtração_4bits_1_cout ), .S(S[7:4]), .Cout(Cout));

  // Other names for the same wires on the sheet: A0[3:0] = A[3:0]; A1[3:0] = A[7:4]; B0[3:0] = B[3:0];
  //   B1[3:0] = B[7:4]; S0[3:0] = S[3:0]; S1[3:0] = S[7:4]
endmodule
