// Digital circuit xor_8bits.dig as structural Verilog
module xor_8bits (
  input  [7:0] A,
  input  [7:0] B,
  output [7:0] S
);

  wire [7:0] and_1_out, and_2_out, not_1_out, not_2_out;

  assign not_1_out = ~A;  // Not not_1, 8 bits wide
  assign not_2_out = ~B;  // Not not_2, 8 bits wide
  assign and_1_out = not_1_out & B;  // And and_1, 8 bits wide
  assign and_2_out = A & not_2_out;  // And and_2, 8 bits wide
  assign S = and_1_out | and_2_out;  // Or or_1, 8 bits wide
endmodule
